# Fritzing sketch RocketLauncher (saved by Fritzing 0.9.3b)
circuit board: 4cm x 5cm
breadboards: 1

parts:
  Q1 = NPN-Transistor [package="TO92 [THT]"]
  Bmicro = Screw terminal - 2 pins [package=THT]
  Blaunch = Screw terminal - 2 pins [package=THT]
  LAUNCH!!! = Screw terminal - 2 pins [package=THT]
  Bmicro_2 = Battery
  RELAY = OMRON PCB Power Relay – G5LE [part_number="G5LE-1\n" package=THT]
  LED = LED - 5mm [color="Red (633nm)" package="5 mm [THT]"]
  220Ω = Resistor [tolerance=±5% resistance=220 package=THT]
  Blaunch_2 = Battery
  220Ω_2 = Resistor [tolerance=±5% resistance=220 package=THT]
  Blend_Micro = Blend Micro v1.0

nets:
  GND: Q1.E, Bmicro.pin2, Bmicro_2.-, LED.cathode, Blend_Micro.GND
  N1: Q1.B, 220Ω_2.Pin_0
  N2: Q1.C, RELAY.COIL2
  N3: Bmicro.pin1, Bmicro_2.+, RELAY.COIL1, Blend_Micro.VIN
  N4: Blaunch.pin1, RELAY.C, Blaunch_2.+
  N5: Blaunch.pin2, LAUNCH!!!.pin2, Blaunch_2.-
  N6: LAUNCH!!!.pin1, RELAY.B
  N7: LED.anode, 220Ω.Pin_0
  N8: 220Ω.Pin_1, Blend_Micro.D9/PWM/A9
  N9: 220Ω_2.Pin_1, Blend_Micro.D8/A8

notes:
  Rocket Launcher
  v1.2 2016.06.27
  github.com/Ehryk/Rockets
